# Fritzing sketch Pi_Zero_DHT11_Oled (saved by Fritzing 0.9.9b)
breadboards: 1

parts:
  MCU1 = Raspberry Pi Zero  # not connected
  Part1 = Adafruit T-Cobbler Plus [part_number="Adafruit #1989 and #2028"]
  OLED_I2C1 = OLED 128x64 I2C Monochrome Display
  DHT1 = DHT11 Humitidy and Temperature Sensor

nets:
  N1: Part1.SDA, OLED_I2C1.SDA
  N2: Part1.SCL, OLED_I2C1.SCK
  GND: Part1.GND, OLED_I2C1.GND, DHT1.NULL
  N3: Part1.GPIO17, DHT1.DATA
  VDD: Part1.+5V, OLED_I2C1.VDD, DHT1.VDD

custom parts:
  Adafruit T-Cobbler Plus: The Raspberry Pi has landed on the Maker World like a 40-GPIO pinned, quad-USB ported, credit card sized bomb of DIY joy. And while you can use most of our great Model B accessories by hooking up our downgrade cable, its probably a good time to upgrade your set up and accessorize using all of the 40 pins. That's why we now carry the Assembled Adafruit Pi T-Cobbler Plus - Breakout + Cable for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
  DHT11 Humitidy and Temperature Sensor: DHT11 Humidity and Temperature Sensor
